# Fritzing sketch biosflash (saved by Fritzing 0.5.2b)
breadboards: 1

parts:
  IC1 = IC, DIP package, 8 pins [chip_label=MX25L spacing=300mil]
  Arduino1 = Arduino

nets:
  N1: IC1.pin1, Arduino1.D10
  N2: IC1.pin2, Arduino1.D12
  N3: IC1.pin3, IC1.pin7, IC1.pin8, Arduino1.+5V
  GND: IC1.pin4, Arduino1.GND
  N4: IC1.pin5, Arduino1.D11
  N5: IC1.pin6, Arduino1.D13
